# Fritzing sketch Example4 (saved by Fritzing 0.9.2b)
breadboards: 1

parts:
  Part1 = Arduino Uno (Rev3)
  LED1 = LED - 5mm [color="Red (633nm)" package="5 mm [THT]"]
  R1 = Resistor [tolerance=±5% resistance=220 package=THT]
  S1 = Pushbutton [package="[THT]"]
  R2 = Resistor [tolerance=±5% resistance=220 package=THT]
  R3 = Rotary Potentiometer (Small) [maximum_resistance=100kΩ package=THT]

nets:
  N1: Part1.A0, R3.wiper
  N2: Part1.D3_PWM, R2.Pin_1
  N3: Part1.D5_PWM, LED1.anode
  N4: Part1.5V, R3.leg2
  N5: Part1.GND, R1.Pin_0, R2.Pin_0, R3.leg1
  N6: LED1.cathode, R1.Pin_1
  N7: S1.Pin_1, S1.Pin_2
  N8: S1.Pin_3, S1.Pin_4
