# Fritzing sketch Example5 (saved by Fritzing 0.9.2b)
breadboards: 1

parts:
  Part1 = Arduino Uno (Rev3)
  DHT2 = DHT11 Humitidy and Temperature Sensor
  R1 = Resistor [tolerance=±5% resistance=220 package="0805 [SMD]"]

nets:
  N1: Part1.D3_PWM, DHT2.DATA, R1.Pin_1
  5V: Part1.5V, DHT2.VDD, R1.Pin_0
  GND: Part1.GND, DHT2.GND

custom parts:
  DHT11 Humitidy and Temperature Sensor: DHT11 Humidity and Temperature Sensor
